# Fritzing sketch Button Sketch (saved by Fritzing 0.9.2b)
circuit board: 8.46667cm x 5.64444cm
breadboards: 1

parts:
  U1 = ESP8266 WiFi Module [part_number=ESP8266]
  D1 = Diode [package=diode-1n4001]
  VCC1 = Battery
  R1 = Resistor [tolerance=±5% resistance=220 package=THT]
  S1 = Pushbutton [package="[THT]"]

nets:
  N1: U1.VCC, VCC1.+, S1.Pin_1, S1.Pin_2
  N2: U1.GPIO_2, R1.Pin_0
  N3: U1.CH_PD, D1.C
  N4: U1.GND, VCC1.-
  N5: D1.A, R1.Pin_1, S1.Pin_3, S1.Pin_4

custom parts:
  ESP8266 WiFi Module: Generic WiFi Module based on the ESP8266 with onboard PCB antenna and UART communications
